// Logisim project CPU.circ as structural Verilog: 9 circuits, main circuit CPU_1T
// REGS
module RegisterBank (
  input  [15:0] DATA_IN,
  input  CHIP_ENABLE,
  input  ZERO_ENABLE,
  input  [2:0] ADDR,
  input  READ_WRITE,
  output [15:0] DATA_OUT
);

  wire clock_1_out, decoder_1_out0, decoder_1_out1, decoder_1_out2, decoder_1_out3, decoder_1_out4,
       decoder_1_out5, decoder_1_out6, decoder_1_out7, not_1_out;
  wire [15:0] controlled_buffer_1_out, controlled_buffer_2_out, multiplexer_1_out, Reg0_q, Reg1_q, Reg2_q,
       Reg3_q, Reg4_q, Reg5_q, Reg6_q, Reg7_q;

  Clock clock_1 (.out(clock_1_out));
  Pull_Resistor pull_resistor_1 (.node(READ_WRITE));
  Decoder #(.select(3), .disabled(0)) decoder_1 (
    .out0(decoder_1_out0), .out1(decoder_1_out1), .out2(decoder_1_out2), .out3(decoder_1_out3),
    .out4(decoder_1_out4), .out5(decoder_1_out5), .out6(decoder_1_out6), .out7(decoder_1_out7), .sel(ADDR),
    .en(READ_WRITE));
  assign controlled_buffer_1_out = CHIP_ENABLE ? DATA_IN : 16'bz;  // Controlled_Buffer controlled_buffer_1
  not not_1 (not_1_out, READ_WRITE);
  assign controlled_buffer_2_out = READ_WRITE ? controlled_buffer_1_out : 16'bz;  // Controlled_Buffer controlled_buffer_2
  Register #(.width(16), .trigger("high")) Reg0 (
    .D(controlled_buffer_2_out), .en(decoder_1_out0), .Q(Reg0_q), .clk(clock_1_out), .clr(ZERO_ENABLE));
  Register #(.width(16), .trigger("high")) Reg1 (
    .D(controlled_buffer_2_out), .en(decoder_1_out1), .Q(Reg1_q), .clk(clock_1_out));  // open: clr
  Register #(.width(16), .trigger("high")) Reg2 (
    .D(controlled_buffer_2_out), .en(decoder_1_out2), .Q(Reg2_q), .clk(clock_1_out));  // open: clr
  Register #(.width(16), .trigger("high")) Reg3 (
    .D(controlled_buffer_2_out), .en(decoder_1_out3), .Q(Reg3_q), .clk(clock_1_out));  // open: clr
  Register #(.width(16), .trigger("high")) Reg4 (
    .D(controlled_buffer_2_out), .en(decoder_1_out4), .Q(Reg4_q), .clk(clock_1_out));  // open: clr
  Register #(.width(16), .trigger("high")) Reg5 (
    .D(controlled_buffer_2_out), .en(decoder_1_out5), .Q(Reg5_q), .clk(clock_1_out));  // open: clr
  Register #(.width(16), .trigger("high")) Reg6 (
    .D(controlled_buffer_2_out), .en(decoder_1_out6), .Q(Reg6_q), .clk(clock_1_out));  // open: clr
  Register #(.width(16), .trigger("high")) Reg7 (
    .D(controlled_buffer_2_out), .en(decoder_1_out7), .Q(Reg7_q), .clk(clock_1_out));  // open: clr
  Pull_Resistor pull_resistor_2 (.node(not_1_out));
  Multiplexer #(.select(3), .width(16)) multiplexer_1 (
    .in0(Reg0_q), .in1(Reg1_q), .in2(Reg2_q), .in3(Reg3_q), .in4(Reg4_q), .in5(Reg5_q), .in6(Reg6_q),
    .in7(Reg7_q), .out(multiplexer_1_out), .sel(ADDR), .en(not_1_out));
  assign DATA_OUT = CHIP_ENABLE ? multiplexer_1_out : 16'bz;  // Controlled_Buffer controlled_buffer_3

  // Notes on the sheet:
  //   ADDR: pull=down
  //   DATA_IN: pull=down
endmodule

module ALU (
  input  [2:0] OPCODE_IN,
  input  READ_WRITE,
  input  [15:0] DATA_IN,
  input  ADDR,
  input  CHIP_ENABLE,
  output [15:0] DATA_OUT,
  output REGA___REGB,
  output REGA___REGB_2,
  output REGA___REGB_3
);

  wire button_1_out, button_2_out, clock_1_out, decoder_1_out0, decoder_1_out1, not_1_out;
  wire [15:0] adder_1_out, controlled_buffer_1_out, controlled_buffer_2_out, multiplexer_1_out, nand_1_out,
       RegA_q, RegB_q;

  Button button_1 (.out(button_1_out));
  Decoder #(.disabled(0)) decoder_1 (.out0(decoder_1_out0), .out1(decoder_1_out1), .sel(ADDR), .en(READ_WRITE));
  Button button_2 (.out(button_2_out));
  assign controlled_buffer_1_out = CHIP_ENABLE ? DATA_IN : 16'bz;  // Controlled_Buffer controlled_buffer_1
  assign controlled_buffer_2_out = READ_WRITE ? controlled_buffer_1_out : 16'bz;  // Controlled_Buffer controlled_buffer_2
  Register #(.width(16), .trigger("high")) RegA (
    .D(controlled_buffer_2_out), .en(decoder_1_out0), .Q(RegA_q), .clk(clock_1_out), .clr(button_1_out));
  Clock clock_1 (.out(clock_1_out));
  Register #(.width(16), .trigger("high")) RegB (
    .D(controlled_buffer_2_out), .en(decoder_1_out1), .Q(RegB_q), .clk(clock_1_out), .clr(button_2_out));
  Adder #(.width(16)) adder_1 (.a(RegA_q), .b(RegB_q), .out(adder_1_out));  // open: cin, cout
  assign nand_1_out = ~(RegA_q & RegB_q);  // NAND_Gate nand_1, 16 bits wide
  Comparator #(.width(16)) comparator_1 (
    .a(RegA_q), .b(RegB_q), .gt(REGA___REGB), .eq(REGA___REGB_2), .lt(REGA___REGB_3));
  not not_1 (not_1_out, READ_WRITE);
  Multiplexer #(.select(3), .width(16)) multiplexer_1 (
    .in0(adder_1_out), .in1(adder_1_out), .in2(nand_1_out), .out(multiplexer_1_out), .sel(OPCODE_IN),
    .en(not_1_out));  // open: in3, in4, in5, in6, in7
  assign DATA_OUT = CHIP_ENABLE ? multiplexer_1_out : 16'bz;  // Controlled_Buffer controlled_buffer_3

  // Notes on the sheet:
  //   CHIP_ENABLE: pull=down
  //   REGA___REGB_3: pull=down
  //   DATA_IN: pull=down
  //   REGA___REGB_2: pull=down
  //   REGA___REGB: pull=down
endmodule

module CPU (
  input  [15:0] DATA_IN,
  output BUS_R_W,
  output [15:0] DATA_OUT,
  output [15:0] ADDRESS_BUS
);

  wire _CLK, A_B, A_B_t, A_B_t_t, ADDR_REG_A_W, ADDR_REG_B_W, ADDR_REG_W_ENABLE, ALU_ENABLE, ALU_R_S,
       ALU_R_W, BUS_ENABLE, CLK, controlled_buffer_8_out, controlled_buffer_9_out, ENA_R_0, ENA_R_1, ENA_R_A,
       ENA_R_B, ENA_R_C, IMM_ENABLE, INSTR_REG_R_W, INSTR_REG_WE, MPG_RST, NOP, not_1_out, not_2_out,
       not_4_out, PC_ENABLE, PGC_INC, PGC_L, PGC_OVF, pull_resistor_17_node, REG_ENABLE, REG_R_W, SEL_RW_0,
       SEL_RW_1, SEL_RW_2;
  wire [1:0] MPG_ADDR;
  wire [2:0] REG_ADDR;
  wire [6:0] bit_extender_1_out, IMM_7;
  wire [9:7] IMM_10;
  wire [13:12] rom_2_data;
  wire [15:0] adder_1_out, bit_extender_2_out, controlled_buffer_5_out, controlled_buffer_7_out,
       controlled_buffer_10_out, controlled_buffer_11_out, counter_2_q, DATA_BUS, PGC;
  wire [15:10] INSTRUCTION;

  RegisterBank RB1 (
    .DATA_IN(DATA_BUS), .DATA_OUT(DATA_BUS), .READ_WRITE(REG_R_W), .ADDR(REG_ADDR), .CHIP_ENABLE(REG_ENABLE),
    .ZERO_ENABLE(1'b1));
  // Probe on INSTRUCTION[12:10]
  assign REG_ADDR = ENA_R_A ? INSTRUCTION[12:10] : 3'bz;  // Controlled_Buffer controlled_buffer_1
  // Probe on IMM_10
  assign REG_ADDR = ENA_R_B ? IMM_10 : 3'bz;  // Controlled_Buffer controlled_buffer_2
  // Probe on IMM_7[2:0]
  assign REG_ADDR = ENA_R_C ? IMM_7[2:0] : 3'bz;  // Controlled_Buffer controlled_buffer_3
  // Probe on INSTRUCTION[15:13]
  // Probe on INSTRUCTION[12:10]
  // Probe on IMM_7
  // Probe on {IMM_10, IMM_7}
  ALU alu_1 (
    .DATA_IN(DATA_BUS), .DATA_OUT(DATA_BUS), .REGA___REGB_2(A_B_t), .ADDR(ALU_R_S), .READ_WRITE(ALU_R_W),
    .OPCODE_IN(INSTRUCTION[15:13]), .CHIP_ENABLE(ALU_ENABLE), .REGA___REGB(A_B_t_t), .REGA___REGB_3(A_B));
  // Probe on DATA_BUS
  // Probe on IMM_10
  // Probe on IMM_7[2:0]
  Decoder #(.select(3), .disabled(0), .enable("false")) decoder_1 (
    .out1(REG_R_W), .out2(ALU_R_W), .out3(BUS_R_W), .out4(PGC_L), .out5(INSTR_REG_R_W), .out6(ADDR_REG_A_W),
    .out7(ADDR_REG_B_W), .sel({SEL_RW_2, SEL_RW_1, SEL_RW_0}));  // open: out0
  // Probe on ADDRESS_BUS
  not not_1 (not_1_out, BUS_R_W);
  assign DATA_OUT = BUS_R_W ? controlled_buffer_7_out : 16'bz;  // Controlled_Buffer controlled_buffer_4
  assign controlled_buffer_5_out = not_1_out ? DATA_IN : 16'bz;  // Controlled_Buffer controlled_buffer_5
  assign DATA_BUS = BUS_ENABLE ? controlled_buffer_5_out : 16'bz;  // Controlled_Buffer controlled_buffer_6
  assign controlled_buffer_7_out = BUS_ENABLE ? DATA_BUS : 16'bz;  // Controlled_Buffer controlled_buffer_7
  ROM #(.addrWidth(16), .dataWidth(16)) rom_1 (.addr(ADDRESS_BUS), .data(DATA_BUS), .sel(PGC_INC));
  Decoder #(.select(2), .disabled(0), .enable("false")) decoder_2 (
    .out1(ENA_R_A), .out2(ENA_R_B), .out3(ENA_R_C), .sel({ENA_R_1, ENA_R_0}));  // open: out0
  // IMM_CONTROLLER IMM_CON: pin names not known; wires that end beside it: DATA_BUS, INSTRUCTION[15:13], IMM_ENABLE, {IMM_10, IMM_7}, IMM_7
  nor nor_1 (NOP, IMM_7[0], IMM_7[1], IMM_7[2], IMM_7[3], IMM_7[4], IMM_7[5], IMM_7[6], IMM_10[7], IMM_10[8], IMM_10[9], INSTRUCTION[10], INSTRUCTION[11], INSTRUCTION[12], INSTRUCTION[13], INSTRUCTION[14], INSTRUCTION[15]);
  // Probe on DATA_BUS
  or or_1 (REG_ENABLE, ENA_R_0, ENA_R_1);
  // Probe on MPG_ADDR
  Counter #(.width(2), .max('h3), .trigger("falling")) counter_1 (
    .Q(MPG_ADDR), .clk(CLK), .clr(controlled_buffer_8_out));  // open: load, D, count, carry
  assign controlled_buffer_8_out = CLK ? MPG_RST : 1'bz;  // Controlled_Buffer controlled_buffer_8
  // Probe on INSTRUCTION[15:13]
  not not_2 (not_2_out, NOP);
  Pull_Resistor pull_resistor_1 (.node(SEL_RW_0));
  Pull_Resistor pull_resistor_2 (.node(ENA_R_0));
  Pull_Resistor pull_resistor_3 (.node(ALU_ENABLE));
  ROM #(.addrWidth(5), .dataWidth(16)) rom_2 (
    .addr({INSTRUCTION[15:13], MPG_ADDR}),
    .data({MPG_RST, PGC_INC, rom_2_data, ADDR_REG_W_ENABLE, IMM_ENABLE, INSTR_REG_WE, PC_ENABLE, BUS_ENABLE, ALU_ENABLE, ALU_R_S, ENA_R_1, ENA_R_0, SEL_RW_2, SEL_RW_1, SEL_RW_0}),
    .sel(not_2_out));
  Pull_Resistor pull_resistor_4 (.node(INSTR_REG_WE));
  Pull_Resistor pull_resistor_5 (.node(rom_2_data[12]));
  Pull_Resistor pull_resistor_6 (.node(MPG_RST));
  Pull_Resistor pull_resistor_7 (.node(SEL_RW_1));
  Pull_Resistor pull_resistor_8 (.node(SEL_RW_2));
  Pull_Resistor pull_resistor_9 (.node(ENA_R_1));
  Pull_Resistor pull_resistor_10 (.node(ALU_R_S));
  Pull_Resistor pull_resistor_11 (.node(BUS_ENABLE));
  Pull_Resistor pull_resistor_12 (.node(PC_ENABLE));
  Pull_Resistor pull_resistor_13 (.node(IMM_ENABLE));
  Pull_Resistor pull_resistor_14 (.node(ADDR_REG_W_ENABLE));
  Pull_Resistor pull_resistor_15 (.node(rom_2_data[13]));
  Pull_Resistor pull_resistor_16 (.node(PGC_INC));
  not not_3 (_CLK, CLK);
  Clock clock_1 (.out(CLK));
  // Probe on DATA_BUS
  // Probe on PGC
  Controlled_Buffer controlled_buffer_9 (.out(controlled_buffer_9_out));  // open: in, en
  ADDR_REG addr_reg_1 (
    .ADDRESS(ADDRESS_BUS), .DATA(DATA_BUS), .REG_A_SELECT(ADDR_REG_A_W), .REG_WE(ADDR_REG_W_ENABLE),
    .OE(BUS_ENABLE), .CLK(CLK), .REG_B_SELECT(ADDR_REG_B_W));
  and and_1 (PGC_L, INSTRUCTION[15], INSTRUCTION[14], ~INSTRUCTION[13], A_B_t, MPG_ADDR[1], ~MPG_ADDR[0]);  // AND_Gate
  // Probe on DATA_BUS
  assign controlled_buffer_10_out = PGC_L ? DATA_BUS : 16'bz;  // Controlled_Buffer controlled_buffer_10
  assign controlled_buffer_11_out = PGC_L ? PGC : 16'bz;  // Controlled_Buffer controlled_buffer_11
  Register #(.width(16), .trigger("high")) register_1 (
    .D(DATA_BUS), .en(INSTR_REG_WE), .Q({INSTRUCTION, IMM_10, IMM_7}), .clk(CLK));  // open: clr
  // Probe on {INSTRUCTION, IMM_10, IMM_7}
  not not_4 (not_4_out, PGC_L);
  Counter #(.width(16), .max('hffff), .ongoal("load"), .trigger("falling")) counter_2 (
    .load(PGC_L), .count(controlled_buffer_9_out), .Q(counter_2_q), .carry(PGC_OVF), .clk(CLK));  // open: D, clr
  assign PGC = not_4_out ? counter_2_q : 16'bz;  // Controlled_Buffer controlled_buffer_12
  Bit_Extender #(.in_width(16), .out_width(7)) bit_extender_1 (.in(controlled_buffer_10_out), .out(bit_extender_1_out));
  assign bit_extender_2_out = {{9{bit_extender_1_out[6]}}, bit_extender_1_out};  // Bit_Extender bit_extender_2
  // Probe on controlled_buffer_11_out
  Pull_Resistor #(.pull(1)) pull_resistor_17 (.node(pull_resistor_17_node));
  Adder #(.width(16)) adder_1 (
    .a(bit_extender_2_out), .b(controlled_buffer_11_out), .out(adder_1_out), .cin(pull_resistor_17_node));  // open: cout
  // Probe on adder_1_out

  // Other names for the same wires on the sheet: IMM_10[6:0] = IMM_7; INSTRUCTION[9:0] = {IMM_10, IMM_7};
  //   RegC[2:0] = IMM_7[2:0]; RegB[2:0] = IMM_10; RegA[2:0] = INSTRUCTION[12:10]; MPG_CTR[1:0] = MPG_ADDR;
  //   MPG_ADDR[4:2] = INSTRUCTION[15:13]; OPCODE[2:0] = INSTRUCTION[15:13]; PGC_W = PGC_L

  // Notes on the sheet:
  //   BUS_R_W: pull=down
  //   DATA_IN: pull=down
endmodule

module Computer (
);

  wire [15:0] ADDRESS_BUS, DATA_BUS;

  // CPU cpu_1: pin names not known; wires that end beside it: DATA_BUS, DATA_BUS, ADDRESS_BUS
endmodule

module ADDR_REG (
  input  [15:0] DATA,
  input  REG_A_SELECT,
  input  REG_B_SELECT,
  input  REG_WE,
  input  OE,
  input  CLK,
  output [15:0] ADDRESS
);

  wire controlled_buffer_1_out, controlled_buffer_2_out;
  wire [15:0] adder_1_out, register_1_q, register_2_q;

  assign controlled_buffer_1_out = REG_A_SELECT ? REG_WE : 1'bz;  // Controlled_Buffer controlled_buffer_1
  Pull_Resistor pull_resistor_1 (.node(controlled_buffer_1_out));
  assign controlled_buffer_2_out = REG_B_SELECT ? REG_WE : 1'bz;  // Controlled_Buffer controlled_buffer_2
  Pull_Resistor pull_resistor_2 (.node(controlled_buffer_2_out));
  Register #(.width(16), .trigger("high")) register_1 (
    .D(DATA), .en(controlled_buffer_1_out), .Q(register_1_q), .clk(CLK));  // open: clr
  Register #(.width(16), .trigger("high")) register_2 (
    .D(DATA), .en(controlled_buffer_2_out), .Q(register_2_q), .clk(CLK));  // open: clr
  Adder #(.width(16)) adder_1 (.a(register_1_q), .b(register_2_q), .out(adder_1_out));  // open: cin, cout
  assign ADDRESS = OE ? adder_1_out : 16'bz;  // Controlled_Buffer controlled_buffer_3
  // Probe on ADDRESS
  // Probe on DATA

  // Other names for the same wires on the sheet: ADDR_REG_A = REG_A_SELECT; ADDR_REG_B = REG_B_SELECT;
  //   ADDR_REG_WE = REG_WE; ADDRESS_BUS[15:0] = ADDRESS; DATA_BUS[15:0] = DATA; OUTPUT_ENABLE = OE

  // Notes on the sheet:
  //   ADDRESS: pull=down
  //   CLK: pull=down
  //   REG_A_SELECT: pull=down
  //   REG_B_SELECT: pull=down
  //   DATA: pull=down
  //   OE: pull=down
  //   REG_WE: pull=down
endmodule

// IMM_CTL
module IMM_CONTROLLER (
  input  [2:0] OPCODE,
  input  [9:0] IMM_10,
  input  [6:0] IMM_7,
  output [15:0] DATA_BUS
);

  wire ADDI, BEQ, IMM_7_ENABLE, IMM_10_ENABLE, LW, SW;
  wire [7:0] decoder_1_out0;

  assign DATA_BUS = IMM_10_ENABLE ? {IMM_10, {6{1'b0}}} : 16'bz;  // Controlled_Buffer controlled_buffer_1
  assign DATA_BUS = IMM_7_ENABLE ? {{9{1'b0}}, IMM_7} : 16'bz;  // Controlled_Buffer controlled_buffer_2
  Decoder #(.select(3), .disabled(0), .enable("false")) decoder_1 (
    .out0(decoder_1_out0[0]), .out1(ADDI), .out2(decoder_1_out0[2]), .out3(IMM_10_ENABLE), .out4(SW),
    .out5(LW), .out6(BEQ), .out7(decoder_1_out0[7]), .sel(OPCODE));
  or or_1 (IMM_7_ENABLE, ADDI, SW, LW, BEQ);

  // Other names for the same wires on the sheet: LUI = IMM_10_ENABLE

  // Notes on the sheet:
  //   IMM_10: pull=down
  //   OPCODE: pull=down
  //   IMM_7: pull=down
  //   DATA_BUS: pull=down
endmodule

module REGS (
  input  [2:0] REG_A_ADDR,
  input  [2:0] REG_B_ADDR,
  input  [2:0] REG_C_ADDR,
  input  CLK,
  input  A_ENA,
  input  A_WE,
  input  [15:0] A_IN,
  input  B_ENA,
  input  B_WE,
  input  [15:0] B_IN,
  input  C_ENA,
  input  C_WE,
  input  [15:0] C_IN,
  input  ADDR_ENA,
  output [15:0] A_OUT,
  output [15:0] B_OUT,
  output [15:0] C_OUT,
  output [15:0] ADDR_HI_WORD_OUT
);

  wire A_0, A_0_WE, A_1, A_1_WE, A_2, A_2_WE, A_3, A_3_WE, A_4, A_4_WE, A_5, A_5_WE, A_6, A_6_WE, A_7,
       A_7_WE, and_1_out, and_2_out, and_3_out, and_4_out, and_5_out, and_6_out, and_7_out, and_8_out,
       and_9_out, and_10_out, and_11_out, and_12_out, and_25_out, and_26_out, and_27_out, and_28_out,
       and_29_out, and_30_out, and_31_out, and_32_out, and_33_out, and_34_out, and_35_out, and_36_out, B_0,
       B_0_WE, B_1, B_1_WE, B_2, B_2_WE, B_3, B_3_WE, B_4, B_4_WE, B_5, B_5_WE, B_6, B_6_WE, B_7, B_7_WE,
       C_0, C_0_WE, C_1, C_1_WE, C_2, C_2_WE, C_3, C_3_WE, C_4, C_4_WE, C_5, C_5_WE, C_6, C_6_WE, C_7,
       C_7_WE, or_1_out, or_2_out, or_3_out, or_4_out, or_9_out, or_10_out, or_11_out, or_12_out;
  wire [1:0] controlled_buffer_15_out, controlled_buffer_17_out, controlled_buffer_19_out,
       controlled_buffer_20_out, controlled_buffer_21_out, controlled_buffer_22_out,
       controlled_buffer_24_out, controlled_buffer_38_out, controlled_buffer_42_out,
       controlled_buffer_45_out, controlled_buffer_46_out, controlled_buffer_47_out,
       controlled_buffer_48_out, pull_resistor_1_node, pull_resistor_2_node, pull_resistor_4_node,
       pull_resistor_6_node, pull_resistor_11_node, pull_resistor_14_node, pull_resistor_15_node,
       pull_resistor_16_node, pull_resistor_18_node, pull_resistor_19_node, pull_resistor_24_node,
       REG_0_IN_SEL, REG_1_IN_SEL, REG_2_IN_SEL, REG_3_IN_SEL, REG_4_IN_SEL, REG_5_IN_SEL, REG_6_IN_SEL,
       REG_7_IN_SEL;
  wire [15:0] multiplexer_1_out, multiplexer_2_out, multiplexer_3_out, multiplexer_4_out, multiplexer_5_out,
       multiplexer_6_out, multiplexer_7_out, multiplexer_8_out, REG_0_q, REG_1_q, REG_2_q, REG_3_q, REG_4_q,
       REG_5_q, REG_6_q, REG_7_q;

  Decoder #(.select(3), .disabled(0)) decoder_1 (
    .out0(A_0), .out1(A_1), .out2(A_2), .out3(A_3), .out4(A_4), .out5(A_5), .out6(A_6), .out7(A_7),
    .sel(REG_A_ADDR), .en(A_ENA));
  Decoder #(.select(3), .disabled(0)) decoder_2 (
    .out0(B_0), .out1(B_1), .out2(B_2), .out3(B_3), .out4(B_4), .out5(B_5), .out6(B_6), .out7(B_7),
    .sel(REG_B_ADDR), .en(B_ENA));
  Decoder #(.select(3), .disabled(0)) decoder_3 (
    .out0(C_0), .out1(C_1), .out2(C_2), .out3(C_3), .out4(C_4), .out5(C_5), .out6(C_6), .out7(C_7),
    .sel(REG_C_ADDR), .en(C_ENA));
  Multiplexer #(.select(2), .width(16), .disabled(0), .enable("false")) multiplexer_1 (
    .in1(A_IN), .in2(B_IN), .in3(C_IN), .out(multiplexer_1_out), .sel(REG_0_IN_SEL));  // open: in0
  or or_1 (or_1_out, A_0_WE, B_0_WE, C_0_WE);
  Multiplexer #(.select(2), .width(16), .disabled(0), .enable("false")) multiplexer_2 (
    .in1(A_IN), .in2(B_IN), .in3(C_IN), .out(multiplexer_2_out), .sel(REG_1_IN_SEL));  // open: in0
  or or_2 (or_2_out, A_1_WE, B_1_WE, C_1_WE);
  Multiplexer #(.select(2), .width(16), .disabled(0), .enable("false")) multiplexer_3 (
    .in1(A_IN), .in2(B_IN), .in3(C_IN), .out(multiplexer_3_out), .sel(REG_2_IN_SEL));  // open: in0
  or or_3 (or_3_out, A_2_WE, B_2_WE, C_2_WE);
  Multiplexer #(.select(2), .width(16), .disabled(0), .enable("false")) multiplexer_4 (
    .in1(A_IN), .in2(B_IN), .in3(C_IN), .out(multiplexer_4_out), .sel(REG_3_IN_SEL));  // open: in0
  or or_4 (or_4_out, A_3_WE, B_3_WE, C_3_WE);
  and and_1 (and_1_out, A_0, ~A_WE);  // AND_Gate
  Register #(.width(16)) REG_0 (.D(multiplexer_1_out), .en(or_1_out), .Q(REG_0_q), .clk(CLK), .clr(1'b1));
  assign A_OUT = and_1_out ? REG_0_q : 16'bz;  // Controlled_Buffer controlled_buffer_1
  and and_2 (and_2_out, A_1, ~A_WE);  // AND_Gate
  Register #(.width(16)) REG_1 (.D(multiplexer_2_out), .en(or_2_out), .Q(REG_1_q), .clk(CLK));  // open: clr
  assign A_OUT = and_2_out ? REG_1_q : 16'bz;  // Controlled_Buffer controlled_buffer_2
  and and_3 (and_3_out, A_2, ~A_WE);  // AND_Gate
  Register #(.width(16)) REG_2 (.D(multiplexer_3_out), .en(or_3_out), .Q(REG_2_q), .clk(CLK));  // open: clr
  assign A_OUT = and_3_out ? REG_2_q : 16'bz;  // Controlled_Buffer controlled_buffer_3
  and and_4 (and_4_out, A_3, ~A_WE);  // AND_Gate
  Register #(.width(16)) REG_3 (.D(multiplexer_4_out), .en(or_4_out), .Q(REG_3_q), .clk(CLK));  // open: clr
  assign A_OUT = and_4_out ? REG_3_q : 16'bz;  // Controlled_Buffer controlled_buffer_4
  and and_5 (and_5_out, B_0, ~B_WE);  // AND_Gate
  assign B_OUT = and_5_out ? REG_0_q : 16'bz;  // Controlled_Buffer controlled_buffer_5
  and and_6 (and_6_out, B_1, ~B_WE);  // AND_Gate
  assign B_OUT = and_6_out ? REG_1_q : 16'bz;  // Controlled_Buffer controlled_buffer_6
  and and_7 (and_7_out, B_2, ~B_WE);  // AND_Gate
  assign B_OUT = and_7_out ? REG_2_q : 16'bz;  // Controlled_Buffer controlled_buffer_7
  and and_8 (and_8_out, B_3, ~B_WE);  // AND_Gate
  assign B_OUT = and_8_out ? REG_3_q : 16'bz;  // Controlled_Buffer controlled_buffer_8
  and and_9 (and_9_out, C_0, ~C_WE);  // AND_Gate
  assign C_OUT = and_9_out ? REG_0_q : 16'bz;  // Controlled_Buffer controlled_buffer_9
  and and_10 (and_10_out, C_1, ~C_WE);  // AND_Gate
  assign C_OUT = and_10_out ? REG_1_q : 16'bz;  // Controlled_Buffer controlled_buffer_10
  and and_11 (and_11_out, C_2, ~C_WE);  // AND_Gate
  assign C_OUT = and_11_out ? REG_2_q : 16'bz;  // Controlled_Buffer controlled_buffer_11
  and and_12 (and_12_out, C_3, ~C_WE);  // AND_Gate
  assign C_OUT = and_12_out ? REG_3_q : 16'bz;  // Controlled_Buffer controlled_buffer_12
  and and_13 (A_0_WE, A_0, A_WE);
  and and_14 (B_0_WE, B_0, B_WE);
  and and_15 (C_0_WE, C_0, C_WE);
  and and_16 (A_1_WE, A_1, A_WE);
  and and_17 (B_1_WE, B_1, B_WE);
  and and_18 (C_1_WE, C_1, C_WE);
  and and_19 (A_2_WE, A_2, A_WE);
  and and_20 (B_2_WE, B_2, B_WE);
  and and_21 (C_2_WE, C_2, C_WE);
  and and_22 (A_3_WE, A_3, A_WE);
  and and_23 (B_3_WE, B_3, B_WE);
  and and_24 (C_3_WE, C_3, C_WE);
  Pull_Resistor pull_resistor_1 (.node(pull_resistor_1_node));
  assign pull_resistor_1_node = A_0_WE ? 2'b01 : 2'bz;  // Controlled_Buffer controlled_buffer_13
  Pull_Resistor pull_resistor_2 (.node(pull_resistor_2_node));
  assign pull_resistor_2_node = B_0_WE ? 2'b10 : 2'bz;  // Controlled_Buffer controlled_buffer_14
  assign controlled_buffer_15_out = C_0_WE ? 2'b11 : 2'bz;  // Controlled_Buffer controlled_buffer_15
  Pull_Resistor pull_resistor_3 (.node(controlled_buffer_15_out));
  assign REG_0_IN_SEL = pull_resistor_1_node | pull_resistor_2_node | controlled_buffer_15_out;  // OR_Gate or_5, 2 bits wide
  Pull_Resistor pull_resistor_4 (.node(pull_resistor_4_node));
  assign pull_resistor_4_node = A_1_WE ? 2'b01 : 2'bz;  // Controlled_Buffer controlled_buffer_16
  assign controlled_buffer_17_out = B_1_WE ? 2'b10 : 2'bz;  // Controlled_Buffer controlled_buffer_17
  Pull_Resistor pull_resistor_5 (.node(controlled_buffer_17_out));
  Pull_Resistor pull_resistor_6 (.node(pull_resistor_6_node));
  assign pull_resistor_6_node = C_1_WE ? 2'b11 : 2'bz;  // Controlled_Buffer controlled_buffer_18
  assign REG_1_IN_SEL = pull_resistor_4_node | controlled_buffer_17_out | pull_resistor_6_node;  // OR_Gate or_6, 2 bits wide
  assign controlled_buffer_19_out = A_2_WE ? 2'b01 : 2'bz;  // Controlled_Buffer controlled_buffer_19
  Pull_Resistor pull_resistor_7 (.node(controlled_buffer_19_out));
  assign controlled_buffer_20_out = B_2_WE ? 2'b10 : 2'bz;  // Controlled_Buffer controlled_buffer_20
  Pull_Resistor pull_resistor_8 (.node(controlled_buffer_20_out));
  assign controlled_buffer_21_out = C_2_WE ? 2'b11 : 2'bz;  // Controlled_Buffer controlled_buffer_21
  Pull_Resistor pull_resistor_9 (.node(controlled_buffer_21_out));
  assign REG_2_IN_SEL = controlled_buffer_19_out | controlled_buffer_20_out | controlled_buffer_21_out;  // OR_Gate or_7, 2 bits wide
  assign controlled_buffer_22_out = A_3_WE ? 2'b01 : 2'bz;  // Controlled_Buffer controlled_buffer_22
  Pull_Resistor pull_resistor_10 (.node(controlled_buffer_22_out));
  Pull_Resistor pull_resistor_11 (.node(pull_resistor_11_node));
  assign pull_resistor_11_node = B_3_WE ? 2'b10 : 2'bz;  // Controlled_Buffer controlled_buffer_23
  assign controlled_buffer_24_out = C_3_WE ? 2'b11 : 2'bz;  // Controlled_Buffer controlled_buffer_24
  Pull_Resistor pull_resistor_12 (.node(controlled_buffer_24_out));
  assign REG_3_IN_SEL = controlled_buffer_22_out | pull_resistor_11_node | controlled_buffer_24_out;  // OR_Gate or_8, 2 bits wide
  Multiplexer #(.select(2), .width(16), .disabled(0), .enable("false")) multiplexer_5 (
    .in1(A_IN), .in2(B_IN), .in3(C_IN), .out(multiplexer_5_out), .sel(REG_4_IN_SEL));  // open: in0
  or or_9 (or_9_out, A_4_WE, B_4_WE, C_4_WE);
  Multiplexer #(.select(2), .width(16), .disabled(0), .enable("false")) multiplexer_6 (
    .in1(A_IN), .in2(B_IN), .in3(C_IN), .out(multiplexer_6_out), .sel(REG_5_IN_SEL));  // open: in0
  or or_10 (or_10_out, A_5_WE, B_5_WE, C_5_WE);
  Multiplexer #(.select(2), .width(16), .disabled(0), .enable("false")) multiplexer_7 (
    .in1(A_IN), .in2(B_IN), .in3(C_IN), .out(multiplexer_7_out), .sel(REG_6_IN_SEL));  // open: in0
  or or_11 (or_11_out, A_6_WE, B_6_WE, C_6_WE);
  Multiplexer #(.select(2), .width(16), .disabled(0), .enable("false")) multiplexer_8 (
    .in1(A_IN), .in2(B_IN), .in3(C_IN), .out(multiplexer_8_out), .sel(REG_7_IN_SEL));  // open: in0
  or or_12 (or_12_out, A_7_WE, B_7_WE, C_7_WE);
  and and_25 (and_25_out, A_4, ~A_WE);  // AND_Gate
  Register #(.width(16)) REG_4 (.D(multiplexer_5_out), .en(or_9_out), .Q(REG_4_q), .clk(CLK));  // open: clr
  assign A_OUT = and_25_out ? REG_4_q : 16'bz;  // Controlled_Buffer controlled_buffer_25
  and and_26 (and_26_out, A_5, ~A_WE);  // AND_Gate
  Register #(.width(16)) REG_5 (.D(multiplexer_6_out), .en(or_10_out), .Q(REG_5_q), .clk(CLK));  // open: clr
  assign A_OUT = and_26_out ? REG_5_q : 16'bz;  // Controlled_Buffer controlled_buffer_26
  and and_27 (and_27_out, A_6, ~A_WE);  // AND_Gate
  Register #(.width(16)) REG_6 (.D(multiplexer_7_out), .en(or_11_out), .Q(REG_6_q), .clk(CLK));  // open: clr
  assign A_OUT = and_27_out ? REG_6_q : 16'bz;  // Controlled_Buffer controlled_buffer_27
  and and_28 (and_28_out, A_7, ~A_WE);  // AND_Gate
  Register #(.width(16)) REG_7 (.D(multiplexer_8_out), .en(or_12_out), .Q(REG_7_q), .clk(CLK));  // open: clr
  assign A_OUT = and_28_out ? REG_7_q : 16'bz;  // Controlled_Buffer controlled_buffer_28
  assign ADDR_HI_WORD_OUT = ADDR_ENA ? REG_7_q : 16'bz;  // Controlled_Buffer controlled_buffer_29
  and and_29 (and_29_out, B_4, ~B_WE);  // AND_Gate
  assign B_OUT = and_29_out ? REG_4_q : 16'bz;  // Controlled_Buffer controlled_buffer_30
  and and_30 (and_30_out, B_5, ~B_WE);  // AND_Gate
  assign B_OUT = and_30_out ? REG_5_q : 16'bz;  // Controlled_Buffer controlled_buffer_31
  and and_31 (and_31_out, B_6, ~B_WE);  // AND_Gate
  assign B_OUT = and_31_out ? REG_6_q : 16'bz;  // Controlled_Buffer controlled_buffer_32
  and and_32 (and_32_out, B_7, ~B_WE);  // AND_Gate
  assign B_OUT = and_32_out ? REG_7_q : 16'bz;  // Controlled_Buffer controlled_buffer_33
  and and_33 (and_33_out, C_4, ~C_WE);  // AND_Gate
  assign C_OUT = and_33_out ? REG_4_q : 16'bz;  // Controlled_Buffer controlled_buffer_34
  and and_34 (and_34_out, C_5, ~C_WE);  // AND_Gate
  assign C_OUT = and_34_out ? REG_5_q : 16'bz;  // Controlled_Buffer controlled_buffer_35
  and and_35 (and_35_out, C_6, ~C_WE);  // AND_Gate
  assign C_OUT = and_35_out ? REG_6_q : 16'bz;  // Controlled_Buffer controlled_buffer_36
  and and_36 (and_36_out, C_7, ~C_WE);  // AND_Gate
  assign C_OUT = and_36_out ? REG_7_q : 16'bz;  // Controlled_Buffer controlled_buffer_37
  and and_37 (A_4_WE, A_4, A_WE);
  and and_38 (B_4_WE, B_4, B_WE);
  and and_39 (C_4_WE, C_4, C_WE);
  and and_40 (A_5_WE, A_5, A_WE);
  and and_41 (B_5_WE, B_5, B_WE);
  and and_42 (C_5_WE, C_5, C_WE);
  and and_43 (A_6_WE, A_6, A_WE);
  and and_44 (B_6_WE, B_6, B_WE);
  and and_45 (C_6_WE, C_6, C_WE);
  and and_46 (A_7_WE, A_7, A_WE);
  and and_47 (B_7_WE, B_7, B_WE);
  and and_48 (C_7_WE, C_7, C_WE);
  assign controlled_buffer_38_out = A_4_WE ? 2'b01 : 2'bz;  // Controlled_Buffer controlled_buffer_38
  Pull_Resistor pull_resistor_13 (.node(controlled_buffer_38_out));
  Pull_Resistor pull_resistor_14 (.node(pull_resistor_14_node));
  assign pull_resistor_14_node = A_5_WE ? 2'b01 : 2'bz;  // Controlled_Buffer controlled_buffer_39
  Pull_Resistor pull_resistor_15 (.node(pull_resistor_15_node));
  assign pull_resistor_15_node = A_6_WE ? 2'b01 : 2'bz;  // Controlled_Buffer controlled_buffer_40
  Pull_Resistor pull_resistor_16 (.node(pull_resistor_16_node));
  assign pull_resistor_16_node = A_7_WE ? 2'b01 : 2'bz;  // Controlled_Buffer controlled_buffer_41
  assign controlled_buffer_42_out = B_4_WE ? 2'b10 : 2'bz;  // Controlled_Buffer controlled_buffer_42
  Pull_Resistor pull_resistor_17 (.node(controlled_buffer_42_out));
  Pull_Resistor pull_resistor_18 (.node(pull_resistor_18_node));
  assign pull_resistor_18_node = C_4_WE ? 2'b11 : 2'bz;  // Controlled_Buffer controlled_buffer_43
  assign REG_4_IN_SEL = controlled_buffer_38_out | controlled_buffer_42_out | pull_resistor_18_node;  // OR_Gate or_13, 2 bits wide
  Pull_Resistor pull_resistor_19 (.node(pull_resistor_19_node));
  assign pull_resistor_19_node = B_5_WE ? 2'b10 : 2'bz;  // Controlled_Buffer controlled_buffer_44
  assign controlled_buffer_45_out = C_5_WE ? 2'b11 : 2'bz;  // Controlled_Buffer controlled_buffer_45
  Pull_Resistor pull_resistor_20 (.node(controlled_buffer_45_out));
  assign REG_5_IN_SEL = pull_resistor_14_node | pull_resistor_19_node | controlled_buffer_45_out;  // OR_Gate or_14, 2 bits wide
  assign controlled_buffer_46_out = B_6_WE ? 2'b10 : 2'bz;  // Controlled_Buffer controlled_buffer_46
  Pull_Resistor pull_resistor_21 (.node(controlled_buffer_46_out));
  assign controlled_buffer_47_out = C_6_WE ? 2'b11 : 2'bz;  // Controlled_Buffer controlled_buffer_47
  Pull_Resistor pull_resistor_22 (.node(controlled_buffer_47_out));
  assign REG_6_IN_SEL = pull_resistor_15_node | controlled_buffer_46_out | controlled_buffer_47_out;  // OR_Gate or_15, 2 bits wide
  assign controlled_buffer_48_out = B_7_WE ? 2'b10 : 2'bz;  // Controlled_Buffer controlled_buffer_48
  Pull_Resistor pull_resistor_23 (.node(controlled_buffer_48_out));
  Pull_Resistor pull_resistor_24 (.node(pull_resistor_24_node));
  assign pull_resistor_24_node = C_7_WE ? 2'b11 : 2'bz;  // Controlled_Buffer controlled_buffer_49
  assign REG_7_IN_SEL = pull_resistor_16_node | controlled_buffer_48_out | pull_resistor_24_node;  // OR_Gate or_16, 2 bits wide

  // Notes on the sheet:
  //   ADDR_ENA: pull=down
  //   ADDR_HI_WORD_OUT: pull=down
  //   A_OUT: pull=down
  //   C_OUT: pull=down
  //   REG_C_ADDR: pull=down
  //   A_WE: pull=down
  //   B_WE: pull=down
  //   REG_B_ADDR: pull=down
  //   REG_A_ADDR: pull=down
  //   C_WE: pull=down
  //   B_OUT: pull=down
  //   B_ENA: pull=down
  //   CLK: pull=down
  //   C_ENA: pull=down
  //   A_ENA: pull=down
endmodule

// CPU
module CPU_1T (
  input  in_1,
  input  in_2,
  input  in_3,
  input  in_4,
  input  in_5,
  input  in_6,
  input  in_7,
  input  [15:0] in_8,
  input  [15:0] in_9,
  input  [15:0] in_10,
  input  in_11,
  input  [15:0] Instruction
);

  wire _CLK, A_ENA, A_WE, ADD, ADDI, ALU_ENA, B_ENA, B_WE, BEQ, C_ENA, C_WE, CLK, JALR, LUI, LW, NAND, SW;
  wire [2:0] A_ADDR, B_ADDR, C_ADDR;
  wire [6:3] IMM_7;
  wire [15:0] A_DATA, B_DATA, C_DATA, controlled_buffer_8_out, controlled_buffer_9_out,
       controlled_buffer_12_out, IMM_DATA;
  wire [15:13] INSTRUCTION_t;

  Clock clock_1 (.out(CLK));
  Decoder #(.select(3), .disabled(0)) decoder_1 (
    .out0(ADD), .out1(ADDI), .out2(NAND), .out3(LUI), .out4(SW), .out5(LW), .out6(BEQ), .out7(JALR),
    .sel(INSTRUCTION_t), .en(CLK));
  not not_1 (_CLK, CLK);
  assign A_WE = in_1 ? in_2 : 1'bz;  // Controlled_Buffer controlled_buffer_1
  Pull_Resistor pull_resistor_1 (.node(A_WE));
  Pull_Resistor pull_resistor_2 (.node(B_WE));
  assign B_WE = in_1 ? in_3 : 1'bz;  // Controlled_Buffer controlled_buffer_2
  assign C_WE = in_1 ? in_4 : 1'bz;  // Controlled_Buffer controlled_buffer_3
  Pull_Resistor pull_resistor_3 (.node(C_WE));
  assign A_ENA = in_1 ? in_5 : 1'bz;  // Controlled_Buffer controlled_buffer_4
  Pull_Resistor pull_resistor_4 (.node(A_ENA));
  assign B_ENA = in_1 ? in_6 : 1'bz;  // Controlled_Buffer controlled_buffer_5
  Pull_Resistor pull_resistor_5 (.node(B_ENA));
  assign C_ENA = in_1 ? in_7 : 1'bz;  // Controlled_Buffer controlled_buffer_6
  Pull_Resistor pull_resistor_6 (.node(C_ENA));
  assign A_DATA = A_WE ? controlled_buffer_8_out : 16'bz;  // Controlled_Buffer controlled_buffer_7
  assign controlled_buffer_8_out = in_1 ? in_8 : 16'bz;  // Controlled_Buffer controlled_buffer_8
  assign controlled_buffer_9_out = in_1 ? in_9 : 16'bz;  // Controlled_Buffer controlled_buffer_9
  assign B_DATA = B_WE ? controlled_buffer_9_out : 16'bz;  // Controlled_Buffer controlled_buffer_10
  assign C_DATA = C_WE ? controlled_buffer_12_out : 16'bz;  // Controlled_Buffer controlled_buffer_11
  assign controlled_buffer_12_out = in_1 ? in_10 : 16'bz;  // Controlled_Buffer controlled_buffer_12
  assign {INSTRUCTION_t, A_ADDR, B_ADDR, IMM_7, C_ADDR} = in_11 ? Instruction : 16'bz;  // Controlled_Buffer controlled_buffer_13
  REGS regs_1 (
    .A_ENA(A_ENA), .A_WE(A_WE), .A_IN(A_DATA), .A_OUT(A_DATA), .B_ENA(B_ENA), .B_WE(B_WE), .B_IN(B_DATA),
    .B_OUT(B_DATA), .C_ENA(C_ENA), .C_WE(C_WE), .C_IN(C_DATA), .C_OUT(C_DATA), .REG_A_ADDR(A_ADDR),
    .REG_B_ADDR(B_ADDR), .REG_C_ADDR(C_ADDR), .CLK(CLK));  // open: ADDR_HI_WORD_OUT, ADDR_ENA
  // Probe on A_ADDR
  // Probe on B_ADDR
  // Probe on C_ADDR
  // Probe on INSTRUCTION_t
  // Probe on IMM_DATA
  IMM_CONTROLLER imm_controller_1 (
    .DATA_BUS(IMM_DATA), .OPCODE(INSTRUCTION_t), .IMM_10({B_ADDR, IMM_7, C_ADDR}), .IMM_7({IMM_7, C_ADDR}));
  // Probe on A_DATA
  // Probe on B_DATA
  // Probe on C_DATA
  ALU_1T alu_1t_1 (.B_IN(B_DATA), .C_IN(C_DATA), .A_OUT(A_DATA), .OPCODE_IN(INSTRUCTION_t), .CLK(ALU_ENA));
  Pull_Resistor pull_resistor_7 (.node(ALU_ENA));
  assign A_ENA = ADD ? 1'b1 : 1'bz;  // Controlled_Buffer controlled_buffer_14
  assign A_WE = ADD ? 1'b1 : 1'bz;  // Controlled_Buffer controlled_buffer_15
  assign B_ENA = ADD ? 1'b1 : 1'bz;  // Controlled_Buffer controlled_buffer_16
  assign C_ENA = ADD ? 1'b1 : 1'bz;  // Controlled_Buffer controlled_buffer_17
  assign ALU_ENA = ADD ? 1'b1 : 1'bz;  // Controlled_Buffer controlled_buffer_18

  // Other names for the same wires on the sheet: IMM_7[2:0] = C_ADDR; IMM_10[9:0] = {B_ADDR, IMM_7, C_ADDR};
  //   INSTRUCTION_t[12:0] = {A_ADDR, B_ADDR, IMM_7, C_ADDR}; OPCODE[2:0] = INSTRUCTION_t

  // Notes on the sheet:
  //   in_4: pull=down
  //   in_6: pull=down
  //   in_1: pull=down
  //   in_8: pull=down
  //   in_7: pull=down
  //   in_5: pull=down
  //   Instruction: pull=down
  //   in_3: pull=down
  //   in_10: pull=down
  //   in_11: pull=down
  //   in_2: pull=down
  //   in_9: pull=down
endmodule

// ALU
module ALU_1T (
  input  [2:0] OPCODE_IN,
  input  CLK,
  input  [15:0] B_IN,
  input  [15:0] C_IN,
  output [15:0] A_OUT
);

  wire [15:0] adder_1_out, nand_1_out;

  Adder #(.width(16)) adder_1 (.a(B_IN), .b(C_IN), .out(adder_1_out));  // open: cin, cout
  assign nand_1_out = ~(B_IN & C_IN);  // NAND_Gate nand_1, 16 bits wide
  Multiplexer #(.select(3), .width(16)) multiplexer_1 (
    .in0(adder_1_out), .in1(adder_1_out), .in2(nand_1_out), .out(A_OUT), .sel(OPCODE_IN), .en(CLK));  // open: in3, in4, in5, in6, in7

  // Notes on the sheet:
  //   CLK: pull=down
  //   B_IN: pull=down
  //   C_IN: pull=down
endmodule
